// Logisim project Byte_wise.circ as structural Verilog: 1 circuit, main circuit main
module main (
  input  HALT,
  input  CNT_CLR,
  input  RAM_CLR,
  input  MAR_CLR,
  input  CLR_ALL
);

  wire CLK_out, controlled_buffer_1_out, d_ff_1_q, decoder_1_out6, decoder_1_out7, not_1_out, or_1_out;
  wire [2:0] counter_1_q;
  wire [5:0] decoder_1_out0;
  wire [7:0] adder_1_out, CNT8_q, controlled_buffer_2_out, controlled_buffer_3_out, controlled_buffer_4_out,
       controlled_buffer_6_out, controlled_buffer_8_out, controlled_buffer_10_out, controlled_buffer_17_out,
       INS_REG_q, MAR_q, REG_X_q, REG_Y_q, REG_Z_q, rom_1_data, subtractor_1_out;
  wire [15:0] rom_2_data;

  Clock CLK (.out(CLK_out));
  assign controlled_buffer_1_out = not_1_out ? CLK_out : 1'bz;  // Controlled_Buffer controlled_buffer_1
  not not_1 (not_1_out, HALT);
  Pull_Resistor pull_resistor_1 (.node(controlled_buffer_1_out));
  Counter CNT8 (
    .load(rom_2_data[14]), .D(controlled_buffer_2_out), .count(rom_2_data[12]), .Q(CNT8_q),
    .clk(controlled_buffer_1_out), .clr(CNT_CLR));  // open: carry
  assign controlled_buffer_2_out = rom_2_data[4] ? CNT8_q : 8'bz;  // Controlled_Buffer controlled_buffer_2
  Register MAR (.D(controlled_buffer_2_out), .en(1'b1), .Q(MAR_q), .clk(controlled_buffer_1_out), .clr(MAR_CLR));
  Decoder #(.select(3)) decoder_1 (
    .out0(decoder_1_out0[0]), .out1(decoder_1_out0[1]), .out2(decoder_1_out0[2]), .out3(decoder_1_out0[3]),
    .out4(decoder_1_out0[4]), .out5(decoder_1_out0[5]), .out6(decoder_1_out6), .out7(decoder_1_out7),
    .sel(counter_1_q), .en(1'b1));
  Counter #(.width(3), .max('h7)) counter_1 (
    .Q(counter_1_q), .clk(controlled_buffer_1_out), .clr(d_ff_1_q));  // open: load, D, count, carry
  ROM rom_1 (.addr(MAR_q), .data(rom_1_data), .sel(1'b1));
  D_Flip_Flop d_ff_1 (
    .clk(controlled_buffer_1_out), .D(rom_2_data[9]), .Q(d_ff_1_q), .reset(CLR_ALL));  // open: Qn, preset, en
  assign controlled_buffer_3_out = rom_2_data[0] ? rom_1_data : 8'bz;  // Controlled_Buffer controlled_buffer_3
  assign controlled_buffer_4_out = rom_2_data[5] ? controlled_buffer_3_out : 8'bz;  // Controlled_Buffer controlled_buffer_4
  assign controlled_buffer_3_out = rom_2_data[1] ? REG_X_q : 8'bz;  // Controlled_Buffer controlled_buffer_5
  assign controlled_buffer_6_out = rom_2_data[6] ? controlled_buffer_3_out : 8'bz;  // Controlled_Buffer controlled_buffer_6
  assign controlled_buffer_3_out = rom_2_data[2] ? REG_Y_q : 8'bz;  // Controlled_Buffer controlled_buffer_7
  assign controlled_buffer_8_out = rom_2_data[7] ? controlled_buffer_3_out : 8'bz;  // Controlled_Buffer controlled_buffer_8
  assign controlled_buffer_3_out = rom_2_data[3] ? REG_Z_q : 8'bz;  // Controlled_Buffer controlled_buffer_9
  assign controlled_buffer_10_out = rom_2_data[9] ? controlled_buffer_3_out : 8'bz;  // Controlled_Buffer controlled_buffer_10
  assign controlled_buffer_3_out = rom_2_data[10] ? adder_1_out : 8'bz;  // Controlled_Buffer controlled_buffer_11
  assign controlled_buffer_3_out = rom_2_data[11] ? subtractor_1_out : 8'bz;  // Controlled_Buffer controlled_buffer_12
  Register REG_X (
    .D(controlled_buffer_4_out), .en(rom_2_data[5]), .Q(REG_X_q), .clk(controlled_buffer_1_out), .clr(CLR_ALL));
  Register REG_Y (
    .D(controlled_buffer_6_out), .en(rom_2_data[6]), .Q(REG_Y_q), .clk(controlled_buffer_1_out), .clr(CLR_ALL));
  Register REG_Z (
    .D(controlled_buffer_8_out), .en(rom_2_data[7]), .Q(REG_Z_q), .clk(controlled_buffer_1_out), .clr(CLR_ALL));
  Register INS_REG (
    .D(controlled_buffer_10_out), .en(rom_2_data[9]), .Q(INS_REG_q), .clk(controlled_buffer_1_out),
    .clr(CLR_ALL));
  Pull_Resistor pull_resistor_2 (.node(controlled_buffer_2_out[7]));
  Pull_Resistor pull_resistor_3 (.node(controlled_buffer_2_out[5]));
  Pull_Resistor pull_resistor_4 (.node(controlled_buffer_2_out[6]));
  Pull_Resistor pull_resistor_5 (.node(controlled_buffer_2_out[4]));
  assign controlled_buffer_2_out[3] = rom_2_data[8] ? INS_REG_q[7] : 1'bz;  // Controlled_Buffer controlled_buffer_13
  assign controlled_buffer_2_out[2] = rom_2_data[8] ? INS_REG_q[6] : 1'bz;  // Controlled_Buffer controlled_buffer_14
  assign controlled_buffer_2_out[1] = rom_2_data[8] ? INS_REG_q[5] : 1'bz;  // Controlled_Buffer controlled_buffer_15
  assign controlled_buffer_2_out[0] = rom_2_data[8] ? INS_REG_q[4] : 1'bz;  // Controlled_Buffer controlled_buffer_16
  Pull_Resistor pull_resistor_6 (.node(controlled_buffer_2_out[0]));
  Pull_Resistor pull_resistor_7 (.node(controlled_buffer_2_out[2]));
  Pull_Resistor pull_resistor_8 (.node(controlled_buffer_2_out[1]));
  Pull_Resistor pull_resistor_9 (.node(controlled_buffer_2_out[3]));
  Adder adder_1 (.a(REG_X_q), .b(REG_Y_q), .out(adder_1_out));  // open: cin, cout
  Subtractor subtractor_1 (.a(REG_X_q), .b(REG_Y_q), .out(subtractor_1_out));  // open: bin, bout
  assign controlled_buffer_17_out = rom_2_data[15] ? controlled_buffer_3_out : 8'bz;  // Controlled_Buffer controlled_buffer_17
  Hex_Digit_Display hex_digit_display_1 (.value(REG_Z_q[7:4]), .dp(1'b0));
  RAM ram_1 (
    .addr(controlled_buffer_2_out), .data(controlled_buffer_17_out), .sel(or_1_out),
    .clk(controlled_buffer_1_out), .ld(rom_2_data[13]), .clr(RAM_CLR));
  assign controlled_buffer_3_out = rom_2_data[13] ? controlled_buffer_17_out : 8'bz;  // Controlled_Buffer controlled_buffer_18
  Hex_Digit_Display hex_digit_display_2 (.value(REG_Z_q[3:0]), .dp(1'b0));
  or or_1 (or_1_out, rom_2_data[13], rom_2_data[15]);
  ROM #(.addrWidth(10), .dataWidth(16)) rom_2 (
    .addr({INS_REG_q[3:0], decoder_1_out0}), .data(rom_2_data));  // open: sel

  // Notes on the sheet:
  //   COUNTER
  //   MAR
  //   MEMORY
  //   contents of rom_1 (hex, n*v repeats v):
  //   f1 e2 4 8 10*0 6 3
  //   REG_X
  //   REG_Y
  //   REG_Z
  //   INS_REG
  //   ALU
  //   RAM
  //   OUTPUT (Z)
  //   M_OUT
  //   RX_OUT
  //   RY_OUT
  //   RZ_OUT
  //   M_IN(B)
  //   RX_IN
  //   RY_IN
  //   RZ_IN
  //   R2M
  //   RINX_IN
  //   A_OUT
  //   S_OUT
  //   CI
  //   RAM_OUT
  //   JMP
  //   RAM_IN
  //   contents of rom_2 (hex, n*v repeats v):
  //   0 10 201 62*0 100 21 0 1000 0 0 0 10 7*0 201 48*0 100 41 0 1000 0 0 0 10 7*0 201 48*0 100 81 0 1000
  //   0 0 0 10 7*0 201 49*0 420 0 1000 0 0 0 10 7*0 201 49*0 820 0 1000 0 0 0 10 7*0 201 49*0 42 0 1000 0
  //   0 0 10 7*0 201 49*0 84 0 1000 0 0 0 10 7*0 201 49*0 82 0 1000 0 0 0 10 7*0 201 49*0 24 0 1000 0 0 0
  //   10 7*0 201 49*0 48 0 1000 0 0 0 10 7*0 201 49*0 28 0 1000 0 0 0 10 7*0 201 49*0 4100 0 1000 0 0 0 10
  //   7*0 201 49*0 8102 0 1000 0 0 0 10 7*0 201 49*0 2140 0 1000 0 0 0 2010 7*0 201
endmodule
