// Logisim project CPU.circ as structural Verilog: 1 circuit, main circuit main
module main (
  input  HALT,
  input  CLR_CNT,
  input  CNT_EN,
  input  CLK_OUT,
  input  MI,
  input  MAR_CLR
);

  wire CLK_out_2, controlled_buffer_1_out, controlled_buffer_2_out, controlled_buffer_3_out,
       controlled_buffer_4_out, controlled_buffer_5_out, controlled_buffer_6_out, controlled_buffer_7_out,
       controlled_buffer_8_out, controlled_buffer_9_out, controlled_buffer_10_out, controlled_buffer_11_out,
       controlled_buffer_12_out, controlled_buffer_13_out, controlled_buffer_14_out,
       controlled_buffer_15_out, controlled_buffer_16_out, controlled_buffer_17_out, d_ff_1_q, d_ff_2_q,
       d_ff_3_q, d_ff_4_q, d_ff_5_q, d_ff_6_q, d_ff_7_q, d_ff_8_q, not_1_out, not_2_out, not_3_out, t_ff_1_q,
       t_ff_1_qn, t_ff_2_q, t_ff_2_qn, t_ff_3_q, t_ff_3_qn, t_ff_4_q, t_ff_4_qn, t_ff_5_q, t_ff_5_qn,
       t_ff_6_q, t_ff_6_qn, t_ff_7_q, t_ff_7_qn, t_ff_8_qn;

  Clock CLK (.out(CLK_out_2));
  not not_1 (not_1_out, HALT);
  assign controlled_buffer_1_out = not_1_out ? CLK_out_2 : 1'bz;  // Controlled_Buffer controlled_buffer_1
  Pull_Resistor pull_resistor_1 (.node(controlled_buffer_1_out));
  not not_2 (not_2_out, controlled_buffer_1_out);
  not not_3 (not_3_out, not_2_out);
  T_Flip_Flop t_ff_1 (
    .clk(not_3_out), .T(1'b1), .Q(t_ff_1_q), .Qn(t_ff_1_qn), .preset(CLR_CNT), .en(CNT_EN));  // open: reset
  assign controlled_buffer_2_out = CLK_OUT ? t_ff_1_qn : 1'bz;  // Controlled_Buffer controlled_buffer_2
  Pull_Resistor pull_resistor_2 (.node(controlled_buffer_2_out));
  assign controlled_buffer_3_out = MI ? controlled_buffer_2_out : 1'bz;  // Controlled_Buffer controlled_buffer_3
  Pull_Resistor pull_resistor_3 (.node(controlled_buffer_3_out));
  T_Flip_Flop t_ff_2 (
    .clk(t_ff_1_q), .T(1'b1), .Q(t_ff_2_q), .Qn(t_ff_2_qn), .preset(CLR_CNT), .en(CNT_EN));  // open: reset
  assign controlled_buffer_4_out = CLK_OUT ? t_ff_2_qn : 1'bz;  // Controlled_Buffer controlled_buffer_4
  Pull_Resistor pull_resistor_4 (.node(controlled_buffer_4_out));
  assign controlled_buffer_5_out = MI ? controlled_buffer_4_out : 1'bz;  // Controlled_Buffer controlled_buffer_5
  D_Flip_Flop d_ff_1 (
    .clk(controlled_buffer_1_out), .D(controlled_buffer_3_out), .Q(d_ff_1_q), .preset(MAR_CLR));  // open: Qn, en, reset
  Pull_Resistor pull_resistor_5 (.node(controlled_buffer_5_out));
  T_Flip_Flop t_ff_3 (
    .clk(t_ff_2_q), .T(1'b1), .Q(t_ff_3_q), .Qn(t_ff_3_qn), .preset(CLR_CNT), .en(CNT_EN));  // open: reset
  assign controlled_buffer_6_out = CLK_OUT ? t_ff_3_qn : 1'bz;  // Controlled_Buffer controlled_buffer_6
  Pull_Resistor pull_resistor_6 (.node(controlled_buffer_6_out));
  assign controlled_buffer_7_out = MI ? controlled_buffer_6_out : 1'bz;  // Controlled_Buffer controlled_buffer_7
  D_Flip_Flop d_ff_2 (
    .clk(controlled_buffer_1_out), .D(controlled_buffer_5_out), .Q(d_ff_2_q), .preset(MAR_CLR));  // open: Qn, en, reset
  Pull_Resistor pull_resistor_7 (.node(controlled_buffer_7_out));
  T_Flip_Flop t_ff_4 (
    .clk(t_ff_3_q), .T(1'b1), .Q(t_ff_4_q), .Qn(t_ff_4_qn), .preset(CLR_CNT), .en(CNT_EN));  // open: reset
  assign controlled_buffer_8_out = CLK_OUT ? t_ff_4_qn : 1'bz;  // Controlled_Buffer controlled_buffer_8
  Pull_Resistor pull_resistor_8 (.node(controlled_buffer_8_out));
  assign controlled_buffer_9_out = MI ? controlled_buffer_8_out : 1'bz;  // Controlled_Buffer controlled_buffer_9
  D_Flip_Flop d_ff_3 (
    .clk(controlled_buffer_1_out), .D(controlled_buffer_7_out), .Q(d_ff_3_q), .preset(MAR_CLR));  // open: Qn, en, reset
  Pull_Resistor pull_resistor_9 (.node(controlled_buffer_9_out));
  T_Flip_Flop t_ff_5 (
    .clk(t_ff_6_q), .T(1'b1), .Q(t_ff_5_q), .Qn(t_ff_5_qn), .preset(CLR_CNT), .en(CNT_EN));  // open: reset
  T_Flip_Flop t_ff_6 (
    .clk(t_ff_4_q), .T(1'b1), .Q(t_ff_6_q), .Qn(t_ff_6_qn), .preset(CLR_CNT), .en(CNT_EN));  // open: reset
  assign controlled_buffer_10_out = CLK_OUT ? t_ff_6_qn : 1'bz;  // Controlled_Buffer controlled_buffer_10
  Pull_Resistor pull_resistor_10 (.node(controlled_buffer_10_out));
  assign controlled_buffer_11_out = MI ? controlled_buffer_10_out : 1'bz;  // Controlled_Buffer controlled_buffer_11
  D_Flip_Flop d_ff_4 (
    .clk(controlled_buffer_1_out), .D(controlled_buffer_9_out), .Q(d_ff_4_q), .preset(MAR_CLR));  // open: Qn, en, reset
  Pull_Resistor pull_resistor_11 (.node(controlled_buffer_11_out));
  T_Flip_Flop t_ff_7 (
    .clk(t_ff_5_q), .T(1'b1), .Q(t_ff_7_q), .Qn(t_ff_7_qn), .preset(CLR_CNT), .en(CNT_EN));  // open: reset
  assign controlled_buffer_12_out = CLK_OUT ? t_ff_5_qn : 1'bz;  // Controlled_Buffer controlled_buffer_12
  assign controlled_buffer_13_out = CLK_OUT ? t_ff_7_qn : 1'bz;  // Controlled_Buffer controlled_buffer_13
  Pull_Resistor pull_resistor_12 (.node(controlled_buffer_12_out));
  assign controlled_buffer_14_out = MI ? controlled_buffer_12_out : 1'bz;  // Controlled_Buffer controlled_buffer_14
  D_Flip_Flop d_ff_5 (
    .clk(controlled_buffer_1_out), .D(controlled_buffer_11_out), .Q(d_ff_5_q), .preset(MAR_CLR));  // open: Qn, en, reset
  Pull_Resistor pull_resistor_13 (.node(controlled_buffer_14_out));
  T_Flip_Flop t_ff_8 (.clk(t_ff_7_q), .T(1'b1), .Qn(t_ff_8_qn), .preset(CLR_CNT), .en(CNT_EN));  // open: Q, reset
  assign controlled_buffer_15_out = CLK_OUT ? t_ff_8_qn : 1'bz;  // Controlled_Buffer controlled_buffer_15
  Pull_Resistor pull_resistor_14 (.node(controlled_buffer_13_out));
  assign controlled_buffer_16_out = MI ? controlled_buffer_13_out : 1'bz;  // Controlled_Buffer controlled_buffer_16
  D_Flip_Flop d_ff_6 (
    .clk(controlled_buffer_1_out), .D(controlled_buffer_14_out), .Q(d_ff_6_q));  // open: Qn, preset, en, reset
  Pull_Resistor pull_resistor_15 (.node(controlled_buffer_16_out));
  Pull_Resistor pull_resistor_16 (.node(controlled_buffer_15_out));
  assign controlled_buffer_17_out = MI ? controlled_buffer_15_out : 1'bz;  // Controlled_Buffer controlled_buffer_17
  D_Flip_Flop d_ff_7 (
    .clk(controlled_buffer_1_out), .D(controlled_buffer_16_out), .Q(d_ff_7_q));  // open: Qn, preset, en, reset
  Pull_Resistor pull_resistor_17 (.node(controlled_buffer_17_out));
  D_Flip_Flop d_ff_8 (
    .clk(controlled_buffer_1_out), .D(controlled_buffer_17_out), .Q(d_ff_8_q));  // open: Qn, preset, en, reset
endmodule
